# Fritzing sketch TwitterHardware (saved by Fritzing 0.2.5)
breadboards: 1

parts:
  Arduino1 = Arduino Diecimila (deprecated) [package=THT]
  R2 = Rotary Potentiometer (Large) [package=THT]
  S1 = Pushbutton [package=THT]
  S2 = Pushbutton [package=THT]
  R5 = 1k Ω Resistor [package=THT]
  R6 = 1k Ω Resistor [package=THT]
  R1 = Rotary Potentiometer (Large) [package=THT]

nets:
  N1: Arduino1.GND, R2.leg2, R5.Pin_1, R6.Pin_1, R1.leg2
  N2: Arduino1.+5V, R2.leg1, S1.leg1, S2.leg0, R1.leg1
  N3: Arduino1.A0, S2.leg1, R5.Pin_0
  N4: Arduino1.A1, S1.leg0, R6.Pin_0
  N5: Arduino1.A2, R1.wiper
